# Fritzing sketch ArduinoSchaltplan (saved by Fritzing 0.9.3b)
breadboards: 2

parts:
  Bauteil1 = Arduino Mega ADK (Rev3)
  Bauteil2 = Soil Moisture Sensor
  R1 = Resistor [tolerance=±5% resistance=1k package="0603 [SMD]"]
  U1 = TRANSISTOR_NPN_2 [package=to-92]
  U2 = LCD-16X2 [package=lcd-16x2]
  R2 = Trimmer Potentiometer [maximum_resistance=10kΩ package=THT]
  R3 = Resistor [tolerance=±5% resistance=220 package="2010 [SMD]"]
  R4 = PHOTOCELL [package=photocell-kit]
  R5 = Resistor [tolerance=±5% resistance=10k package=THT]
  DHT1 = DHT11 Humitidy and Temperature Sensor
  R6 = Resistor [tolerance=±5% resistance=10k package="0402 [SMD]"]
  ZS-042_RTC1 = ZS-042 RTC Module
  LED1 = LEDs [package=led10mm]
  M2 = DC Motor
  KY-1 = Keyes Relay [package=THT]
  KY-2 = Keyes Relay [package=THT]

nets:
  N1: Bauteil1.A0, Bauteil2.SIG
  N2: Bauteil1.A1, R4.P$1, R5.Pin_1
  N3: Bauteil1.D21/SCL, ZS-042_RTC1.SCL
  N4: Bauteil1.D20/SDA, ZS-042_RTC1.SDA
  GND: Bauteil1.GND, Bauteil2.GND, U2.VSS, U2.R_W, U2.K, R2.leg1, R5.Pin_0, DHT1.GND, ZS-042_RTC1.GND, KY-1.ground, KY-2.ground
  N5: Bauteil1.D13_PWM, U2.RS
  N6: Bauteil1.D12_PWM, U2.E
  N7: Bauteil1.D8_PWM, KY-2.signal
  VDD: Bauteil1.5V, U1.E, U2.VDD, R2.leg2, R3.Pin_1, R4.P$2, DHT1.VDD, R6.Pin_1, ZS-042_RTC1.VCC, KY-2.power
  N8: Bauteil1.D2_PWM, KY-1.signal
  N9: Bauteil1.D3_PWM, R6.Pin_0
  N10: Bauteil1.D4_PWM, U2.DB7
  N11: Bauteil1.D5_PWM, U2.DB6
  N12: Bauteil1.D6_PWM, U2.DB5
  N13: Bauteil1.D7_PWM, U2.DB4
  N14: Bauteil1.D52/SCK, R1.Pin_0
  N15: Bauteil2.VCC, U1.C
  N16: R1.Pin_1, U1.B
  N17: U2.VO, R2.wiper
  N18: U2.A, R3.Pin_0
  N19: LED1.C, KY-1.NO
  N20: M2.pin_2, KY-2.NO

notes:
  Light 230V
  Pump 230V
  Outlet 230V
  Moisture Sensor
  Photoresistor
  10k Ohm Resistor
  DHT11
  10k Ohm Resisotor
  Real-Time-Clock Module
  LCD 16x2

custom parts:
  DHT11 Humitidy and Temperature Sensor: DHT11 Humidity and Temperature Sensor
  LEDs: LEDs Standard schematic elements and footprints for 5mm, 3mm, 1206, and 0603 sized LEDs. 5mm - Spark Fun Electronics SKU : COM-00529 (and others)
  Keyes Relay: The Keyes 5V relay module is suitable for SCM development, home appliance control. It uses a 5V~12V TIL control signal which can control DC / AC signal.
